# Fritzing sketch Layout-Wemos-ProtoBoard (saved by Fritzing 0.9.3b)
breadboards: 1

parts:
  WeMos_D1_Mini_Protoboard_Shield1 = WeMos D1 Mini Protoboard Shield
  WeMos_D1_Mini2 = WeMos D1 Mini
  R1 = Resistor [tolerance=±5% resistance=100 package=THT]
  R2 = Resistor [tolerance=±5% resistance=100 package=THT]
  JP1 = Header 8 [package=1x08_smd]
  JP2 = Header 8 [package=1x08_smd]
  R3 = Resistor [tolerance=±5% resistance=100 package=THT]
  R4 = Resistor [tolerance=±5% resistance=100 package=THT]
  JP3 = Header 8 [package=1x08_smd]
  JP4 = Header 8 [package=1x08_smd]
  WeMos_D1_Mini_Protoboard_Shield2 = WeMos D1 Mini Protoboard Shield
  JP5 = Header 8 [package=1x08_smd]
  JP6 = Header 8 [package=1x08_smd]
  WeMos_D1_Mini_Protoboard_Shield3 = WeMos D1 Mini Protoboard Shield
  R7 = Resistor [tolerance=±5% resistance=100 package=THT]
  R8 = Resistor [tolerance=±5% resistance=100 package=THT]
  JP8 = Header 8 [package=1x08_smd]
  SW1 = DIP SWITCH [package=dipswitch-02]
  S1 = NKK M2032SS1W01 3PDT Toggle Switch [part_number=M2032SS1W01 package=THT]
  JP11 = Header 6 [package=1x06_smd_straight_alt]
  JP7 = Header 8 [package=1x08_smd]
  WeMos_D1_Mini_Protoboard_Shield4 = WeMos D1 Mini Protoboard Shield
  JP12 = Header 6 [package=1x06_smd_straight_alt]

nets:
  N1: WeMos_D1_Mini_Protoboard_Shield1.D1, WeMos_D1_Mini_Protoboard_Shield1.X7-Y3, R3.Pin_1
  N2: WeMos_D1_Mini_Protoboard_Shield1.D2, WeMos_D1_Mini_Protoboard_Shield1.X7-Y4, R4.Pin_1
  N3: WeMos_D1_Mini_Protoboard_Shield1.X2-Y10, JP4.1
  N4: WeMos_D1_Mini_Protoboard_Shield1.X2-Y11, JP3.1
  N5: WeMos_D1_Mini_Protoboard_Shield1.X3-Y3, R3.Pin_0
  N6: WeMos_D1_Mini_Protoboard_Shield1.X3-Y4, R4.Pin_0
  N7: WeMos_D1_Mini_Protoboard_Shield1.X3-Y10, JP4.2
  N8: WeMos_D1_Mini_Protoboard_Shield1.X3-Y11, JP3.2
  N9: WeMos_D1_Mini_Protoboard_Shield1.X4-Y10, JP4.3
  N10: WeMos_D1_Mini_Protoboard_Shield1.X4-Y11, JP3.3
  N11: WeMos_D1_Mini_Protoboard_Shield1.X5-Y10, JP4.4
  N12: WeMos_D1_Mini_Protoboard_Shield1.X5-Y11, JP3.4
  N13: WeMos_D1_Mini_Protoboard_Shield1.X6-Y10, JP4.5
  N14: WeMos_D1_Mini_Protoboard_Shield1.X6-Y11, JP3.5
  N15: WeMos_D1_Mini_Protoboard_Shield1.X7-Y10, JP4.6
  N16: WeMos_D1_Mini_Protoboard_Shield1.X7-Y11, JP3.6
  N17: WeMos_D1_Mini_Protoboard_Shield1.X8-Y10, JP4.7
  N18: WeMos_D1_Mini_Protoboard_Shield1.X8-Y11, JP3.7
  N19: WeMos_D1_Mini_Protoboard_Shield1.X9-Y10, JP4.8
  N20: WeMos_D1_Mini_Protoboard_Shield1.X9-Y11, JP3.8
  N21: WeMos_D1_Mini2.5V, JP1.5, JP2.5
  N22: WeMos_D1_Mini2.D1, JP2.3
  N23: WeMos_D1_Mini2.D2, JP2.1
  N24: WeMos_D1_Mini2.D5, JP1.3
  N25: WeMos_D1_Mini2.D6, JP1.1
  N26: WeMos_D1_Mini2.D7, JP1.8
  N27: WeMos_D1_Mini2.G, R1.Pin_1, R2.Pin_1, JP1.6, JP2.6
  N28: WeMos_D1_Mini2.RX, JP2.8
  N29: WeMos_D1_Mini_Protoboard_Shield2.5V, WeMos_D1_Mini_Protoboard_Shield2.X7-Y8, WeMos_D1_Mini_Protoboard_Shield2.X8-Y10, WeMos_D1_Mini_Protoboard_Shield2.X8-Y11, JP5.2, JP6.2
  N30: WeMos_D1_Mini_Protoboard_Shield2.D1, WeMos_D1_Mini_Protoboard_Shield2.X4-Y10, WeMos_D1_Mini_Protoboard_Shield2.X7-Y3, JP6.6
  N31: WeMos_D1_Mini_Protoboard_Shield2.D2, WeMos_D1_Mini_Protoboard_Shield2.X3-Y10, WeMos_D1_Mini_Protoboard_Shield2.X7-Y4, JP6.7
  N32: WeMos_D1_Mini_Protoboard_Shield2.D5, WeMos_D1_Mini_Protoboard_Shield2.X2-Y4, WeMos_D1_Mini_Protoboard_Shield2.X4-Y11, JP5.6
  N33: WeMos_D1_Mini_Protoboard_Shield2.D6, WeMos_D1_Mini_Protoboard_Shield2.X2-Y5, WeMos_D1_Mini_Protoboard_Shield2.X3-Y11, JP5.7
  N34: WeMos_D1_Mini_Protoboard_Shield2.D7, WeMos_D1_Mini_Protoboard_Shield2.X2-Y6, WeMos_D1_Mini_Protoboard_Shield2.X2-Y11, JP5.8
  N35: WeMos_D1_Mini_Protoboard_Shield2.G, WeMos_D1_Mini_Protoboard_Shield2.X3-Y3, WeMos_D1_Mini_Protoboard_Shield2.X3-Y4, WeMos_D1_Mini_Protoboard_Shield2.X7-Y7, WeMos_D1_Mini_Protoboard_Shield2.X7-Y10, WeMos_D1_Mini_Protoboard_Shield2.X7-Y11, JP5.3, JP6.3
  N36: WeMos_D1_Mini_Protoboard_Shield2.X2-Y10, JP6.8
  N37: WeMos_D1_Mini_Protoboard_Shield2.X5-Y10, JP6.5
  N38: WeMos_D1_Mini_Protoboard_Shield2.X5-Y11, JP5.5
  N39: WeMos_D1_Mini_Protoboard_Shield2.X6-Y10, JP6.4
  N40: WeMos_D1_Mini_Protoboard_Shield2.X6-Y11, JP5.4
  N41: WeMos_D1_Mini_Protoboard_Shield2.X9-Y10, JP6.1
  N42: WeMos_D1_Mini_Protoboard_Shield2.X9-Y11, JP5.1
  N43: WeMos_D1_Mini_Protoboard_Shield3.5V, WeMos_D1_Mini_Protoboard_Shield3.X7-Y8, SW1.1
  N44: WeMos_D1_Mini_Protoboard_Shield3.D1, WeMos_D1_Mini_Protoboard_Shield3.X7-Y3, R8.Pin_1
  N45: WeMos_D1_Mini_Protoboard_Shield3.D2, WeMos_D1_Mini_Protoboard_Shield3.X7-Y4, R7.Pin_1
  N46: WeMos_D1_Mini_Protoboard_Shield3.G, WeMos_D1_Mini_Protoboard_Shield3.X7-Y7, SW1.2
  N47: WeMos_D1_Mini_Protoboard_Shield3.X2-Y10, JP7.1
  N48: WeMos_D1_Mini_Protoboard_Shield3.X2-Y11, JP8.1
  N49: WeMos_D1_Mini_Protoboard_Shield3.X3-Y3, R8.Pin_0
  N50: WeMos_D1_Mini_Protoboard_Shield3.X3-Y4, R7.Pin_0
  N51: WeMos_D1_Mini_Protoboard_Shield3.X3-Y10, JP7.2
  N52: WeMos_D1_Mini_Protoboard_Shield3.X3-Y11, JP8.2
  N53: WeMos_D1_Mini_Protoboard_Shield3.X4-Y7, SW1.3
  N54: WeMos_D1_Mini_Protoboard_Shield3.X4-Y8, SW1.4
  N55: WeMos_D1_Mini_Protoboard_Shield3.X4-Y10, JP7.3
  N56: WeMos_D1_Mini_Protoboard_Shield3.X4-Y11, JP8.3
  N57: WeMos_D1_Mini_Protoboard_Shield3.X5-Y10, JP7.4
  N58: WeMos_D1_Mini_Protoboard_Shield3.X5-Y11, JP8.4
  N59: WeMos_D1_Mini_Protoboard_Shield3.X6-Y10, JP7.5
  N60: WeMos_D1_Mini_Protoboard_Shield3.X6-Y11, JP8.5
  N61: WeMos_D1_Mini_Protoboard_Shield3.X7-Y10, JP7.6
  N62: WeMos_D1_Mini_Protoboard_Shield3.X7-Y11, JP8.6
  N63: WeMos_D1_Mini_Protoboard_Shield3.X8-Y10, JP7.7
  N64: WeMos_D1_Mini_Protoboard_Shield3.X8-Y11, JP8.7
  N65: WeMos_D1_Mini_Protoboard_Shield3.X9-Y10, JP7.8
  N66: WeMos_D1_Mini_Protoboard_Shield3.X9-Y11, JP8.8
  N67: S1.L1-1, WeMos_D1_Mini_Protoboard_Shield4.D1, WeMos_D1_Mini_Protoboard_Shield4.X5-Y10, WeMos_D1_Mini_Protoboard_Shield4.X7-Y3, JP12.4
  N68: S1.C1, JP11.4, WeMos_D1_Mini_Protoboard_Shield4.X5-Y11
  N69: S1.L1-2, WeMos_D1_Mini_Protoboard_Shield4.D5, WeMos_D1_Mini_Protoboard_Shield4.X2-Y4
  N70: S1.L2-1, WeMos_D1_Mini_Protoboard_Shield4.D2, WeMos_D1_Mini_Protoboard_Shield4.X4-Y10, WeMos_D1_Mini_Protoboard_Shield4.X7-Y4, JP12.5
  N71: S1.C2, JP11.5, WeMos_D1_Mini_Protoboard_Shield4.X4-Y11
  N72: S1.L2-2, WeMos_D1_Mini_Protoboard_Shield4.D6, WeMos_D1_Mini_Protoboard_Shield4.X2-Y5
  N73: S1.C3, JP11.2, WeMos_D1_Mini_Protoboard_Shield4.X7-Y10, WeMos_D1_Mini_Protoboard_Shield4.X7-Y11, JP12.2
  N74: S1.L3-2, WeMos_D1_Mini_Protoboard_Shield4.X3-Y8
  N75: JP11.1, WeMos_D1_Mini_Protoboard_Shield4.X3-Y7, WeMos_D1_Mini_Protoboard_Shield4.X8-Y10, WeMos_D1_Mini_Protoboard_Shield4.X8-Y11, JP12.1
  N76: JP11.3, WeMos_D1_Mini_Protoboard_Shield4.X6-Y11
  N77: JP11.6, WeMos_D1_Mini_Protoboard_Shield4.D7, WeMos_D1_Mini_Protoboard_Shield4.X2-Y6, WeMos_D1_Mini_Protoboard_Shield4.X3-Y11
  N78: WeMos_D1_Mini_Protoboard_Shield4.X3-Y3, WeMos_D1_Mini_Protoboard_Shield4.X3-Y4, WeMos_D1_Mini_Protoboard_Shield4.X7-Y7
  N79: WeMos_D1_Mini_Protoboard_Shield4.X3-Y10, JP12.6
  N80: WeMos_D1_Mini_Protoboard_Shield4.X6-Y10, JP12.3

notes:
  Front & Back
  Wemos ProtoBoard
  Front & Back
  Wemos ProtoBoard & Switch
  First try with Protoboard

custom parts:
  NKK M2032SS1W01 3PDT Toggle Switch: NKK M2032SS1W01 3PDT Toggle Switch This switch has three poles and two position
