# Fritzing sketch RoboDesk (saved by Fritzing 0.9.3b)
breadboards: 1

parts:
  WeMos_D1_Mini_Protoboard_Shield1 = WeMos D1 Mini Protoboard Shield
  WeMos_D1_Mini2 = WeMos D1 Mini
  R1 = Resistor [tolerance=±5% resistance=100 package=THT]
  R2 = Resistor [tolerance=±5% resistance=100 package=THT]
  JP1 = Header 8 [package=1x08_smd]
  JP2 = Header 8 [package=1x08_smd]
  R3 = Resistor [tolerance=±5% resistance=100 package=THT]
  R4 = Resistor [tolerance=±5% resistance=100 package=THT]
  JP3 = Header 8 [package=1x08_smd]
  JP4 = Header 8 [package=1x08_smd]
  WeMos_D1_Mini_Protoboard_Shield2 = WeMos D1 Mini Protoboard Shield
  JP5 = Header 8 [package=1x08_smd]
  JP6 = Header 8 [package=1x08_smd]
  R5 = Resistor [tolerance=±5% resistance=100 package=THT]
  R6 = Resistor [tolerance=±5% resistance=100 package=THT]

nets:
  N1: WeMos_D1_Mini_Protoboard_Shield1.D1, WeMos_D1_Mini_Protoboard_Shield1.X7-Y3, R3.Pin_1
  N2: WeMos_D1_Mini_Protoboard_Shield1.D2, WeMos_D1_Mini_Protoboard_Shield1.X7-Y4, R4.Pin_1
  N3: WeMos_D1_Mini_Protoboard_Shield1.X2-Y10, JP4.1
  N4: WeMos_D1_Mini_Protoboard_Shield1.X2-Y11, JP3.1
  N5: WeMos_D1_Mini_Protoboard_Shield1.X3-Y3, R3.Pin_0
  N6: WeMos_D1_Mini_Protoboard_Shield1.X3-Y4, R4.Pin_0
  N7: WeMos_D1_Mini_Protoboard_Shield1.X3-Y10, JP4.2
  N8: WeMos_D1_Mini_Protoboard_Shield1.X3-Y11, JP3.2
  N9: WeMos_D1_Mini_Protoboard_Shield1.X4-Y10, JP4.3
  N10: WeMos_D1_Mini_Protoboard_Shield1.X4-Y11, JP3.3
  N11: WeMos_D1_Mini_Protoboard_Shield1.X5-Y10, JP4.4
  N12: WeMos_D1_Mini_Protoboard_Shield1.X5-Y11, JP3.4
  N13: WeMos_D1_Mini_Protoboard_Shield1.X6-Y10, JP4.5
  N14: WeMos_D1_Mini_Protoboard_Shield1.X6-Y11, JP3.5
  N15: WeMos_D1_Mini_Protoboard_Shield1.X7-Y10, JP4.6
  N16: WeMos_D1_Mini_Protoboard_Shield1.X7-Y11, JP3.6
  N17: WeMos_D1_Mini_Protoboard_Shield1.X8-Y10, JP4.7
  N18: WeMos_D1_Mini_Protoboard_Shield1.X8-Y11, JP3.7
  N19: WeMos_D1_Mini_Protoboard_Shield1.X9-Y10, JP4.8
  N20: WeMos_D1_Mini_Protoboard_Shield1.X9-Y11, JP3.8
  N21: WeMos_D1_Mini2.5V, JP1.5, JP2.5
  N22: WeMos_D1_Mini2.D1, JP2.3
  N23: WeMos_D1_Mini2.D2, JP2.1
  N24: WeMos_D1_Mini2.D5, JP1.3
  N25: WeMos_D1_Mini2.D6, JP1.1
  N26: WeMos_D1_Mini2.D7, JP1.8
  N27: WeMos_D1_Mini2.G, R1.Pin_1, R2.Pin_1, JP1.6, JP2.6
  N28: WeMos_D1_Mini2.RX, JP2.8
  N29: WeMos_D1_Mini_Protoboard_Shield2.5V, WeMos_D1_Mini_Protoboard_Shield2.X7-Y8, WeMos_D1_Mini_Protoboard_Shield2.X8-Y10, WeMos_D1_Mini_Protoboard_Shield2.X8-Y11, JP5.2, JP6.2
  N30: WeMos_D1_Mini_Protoboard_Shield2.D1, WeMos_D1_Mini_Protoboard_Shield2.X4-Y10, WeMos_D1_Mini_Protoboard_Shield2.X7-Y3, JP6.6, R5.Pin_0
  N31: WeMos_D1_Mini_Protoboard_Shield2.D2, WeMos_D1_Mini_Protoboard_Shield2.X3-Y10, WeMos_D1_Mini_Protoboard_Shield2.X7-Y4, JP6.7, R6.Pin_0
  N32: WeMos_D1_Mini_Protoboard_Shield2.D5, WeMos_D1_Mini_Protoboard_Shield2.X2-Y4, WeMos_D1_Mini_Protoboard_Shield2.X4-Y11, JP5.6
  N33: WeMos_D1_Mini_Protoboard_Shield2.D6, WeMos_D1_Mini_Protoboard_Shield2.X2-Y5, WeMos_D1_Mini_Protoboard_Shield2.X3-Y11, JP5.7
  N34: WeMos_D1_Mini_Protoboard_Shield2.D7, WeMos_D1_Mini_Protoboard_Shield2.X2-Y6, WeMos_D1_Mini_Protoboard_Shield2.X2-Y11, JP5.8
  N35: WeMos_D1_Mini_Protoboard_Shield2.G, WeMos_D1_Mini_Protoboard_Shield2.X3-Y3, WeMos_D1_Mini_Protoboard_Shield2.X3-Y4, WeMos_D1_Mini_Protoboard_Shield2.X7-Y7, WeMos_D1_Mini_Protoboard_Shield2.X7-Y10, WeMos_D1_Mini_Protoboard_Shield2.X7-Y11, JP5.3, JP6.3, R5.Pin_1, R6.Pin_1
  N36: WeMos_D1_Mini_Protoboard_Shield2.X2-Y10, JP6.8
  N37: WeMos_D1_Mini_Protoboard_Shield2.X5-Y10, JP6.5
  N38: WeMos_D1_Mini_Protoboard_Shield2.X5-Y11, JP5.5
  N39: WeMos_D1_Mini_Protoboard_Shield2.X6-Y10, JP6.4
  N40: WeMos_D1_Mini_Protoboard_Shield2.X6-Y11, JP5.4
  N41: WeMos_D1_Mini_Protoboard_Shield2.X9-Y10, JP6.1
  N42: WeMos_D1_Mini_Protoboard_Shield2.X9-Y11, JP5.1

notes:
  Front & Back
  Wemos ProtoBoard
